# Fritzing sketch AlexaLPD8806 (saved by Fritzing 0.9.3b)

parts:
  U1 = ESP8266 WiFi Module [part_number=ESP8266]
  LPD8806_RGB_LED_Strip1 = LPD8806 RGB LED Strip
  U2 = Voltage Regulator - 3.3V [package="TO220 [THT]"]
  Power_plug1 = Power plug

nets:
  N1: U1.VCC, U1.CH_PD, U2.output_voltage
  N2: U1.GPIO_0, LPD8806_RGB_LED_Strip1.DI
  N3: U1.GPIO_2, LPD8806_RGB_LED_Strip1.CI
  GND: U1.GND, LPD8806_RGB_LED_Strip1.GND, U2.GND, Power_plug1.GND
  +5V: LPD8806_RGB_LED_Strip1.+5V, U2.input_voltage, Power_plug1.VCC

notes:
  +5V/8A
  GND

custom parts:
  ESP8266 WiFi Module: Generic WiFi Module based on the ESP8266 with onboard PCB antenna and UART communications
  LPD8806 RGB LED Strip: Digitally addressable RGB LED strip
